// Logisim project cpu.circ as structural Verilog: 9 circuits, main circuit d-latch
module d_latch (
  input  enabler,
  input  \input ,
  output Q,
  output Q_prime
);

  wire and_1_out, and_2_out, not_1_out;

  not not_1 (not_1_out, \input );
  and and_1 (and_1_out, not_1_out, enabler);
  and and_2 (and_2_out, enabler, \input );
  nor nor_1 (Q, and_1_out, Q_prime);
  nor nor_2 (Q_prime, Q, and_2_out);
endmodule

module d_flip_flop (
  input  d,
  input  e,
  output q,
  output q_prime
);

  wire d_latch_1_q_prime, not_1_out, not_2_out;

  d_latch d_latch_1 (.Q_prime(d_latch_1_q_prime), .\input (d), .enabler(not_1_out));  // open: Q
  not not_1 (not_1_out, e);
  not not_2 (not_2_out, not_1_out);
  d_latch d_latch_2 (.Q(q), .Q_prime(q_prime), .\input (d_latch_1_q_prime), .enabler(not_2_out));
endmodule

module full_adder_1_bit (
  input  input_1_1_bit,
  input  input_2_1_bit,
  input  carry_in,
  output carry_out,
  output result
);

  wire and_1_out, and_2_out, and_3_out;

  and and_1 (and_1_out, input_1_1_bit, input_2_1_bit);
  and and_2 (and_2_out, input_2_1_bit, carry_in);
  and and_3 (and_3_out, input_1_1_bit, carry_in);
  ExactlyOne xor_1 (.out(result), .in0(input_1_1_bit), .in1(input_2_1_bit), .in2(carry_in));
  or or_1 (carry_out, and_1_out, and_2_out, and_3_out);
endmodule

module full_adder_4_bit (
  input  [3:0] input1_4_bit,
  input  [3:0] input2_4_bit,
  input  carry_in,
  output carry_out,
  output [3:0] \output 
);

  wire full_adder_1_bit_2_carry_out, full_adder_1_bit_3_carry_out, full_adder_1_bit_4_carry_out;

  full_adder_1_bit full_adder_1_bit_1 (
    .input_1_1_bit(input1_4_bit[3]), .input_2_1_bit(input2_4_bit[3]),
    .carry_in(full_adder_1_bit_2_carry_out), .carry_out(carry_out), .result(\output [3]));
  full_adder_1_bit full_adder_1_bit_2 (
    .input_1_1_bit(input1_4_bit[2]), .input_2_1_bit(input2_4_bit[2]),
    .carry_in(full_adder_1_bit_3_carry_out), .carry_out(full_adder_1_bit_2_carry_out), .result(\output [2]));
  full_adder_1_bit full_adder_1_bit_3 (
    .input_1_1_bit(input1_4_bit[1]), .input_2_1_bit(input2_4_bit[1]),
    .carry_in(full_adder_1_bit_4_carry_out), .carry_out(full_adder_1_bit_3_carry_out), .result(\output [1]));
  full_adder_1_bit full_adder_1_bit_4 (
    .input_1_1_bit(input1_4_bit[0]), .input_2_1_bit(input2_4_bit[0]), .carry_in(carry_in),
    .carry_out(full_adder_1_bit_4_carry_out), .result(\output [0]));
endmodule

module full_adder_16_bit (
  input  [15:0] input_1_16_bit,
  input  [15:0] input__16_bit,
  input  carry_in,
  output carry_out,
  output [15:0] \output 
);

  wire full_adder_4_bit_2_carry_out, full_adder_4_bit_3_carry_out, full_adder_4_bit_4_carry_out;

  full_adder_4_bit full_adder_4_bit_1 (
    .input1_4_bit(input_1_16_bit[15:12]), .input2_4_bit(input__16_bit[15:12]),
    .carry_in(full_adder_4_bit_2_carry_out), .carry_out(carry_out), .\output (\output [15:12]));
  full_adder_4_bit full_adder_4_bit_2 (
    .input1_4_bit(input_1_16_bit[11:8]), .input2_4_bit(input__16_bit[11:8]),
    .carry_in(full_adder_4_bit_3_carry_out), .carry_out(full_adder_4_bit_2_carry_out),
    .\output (\output [11:8]));
  full_adder_4_bit full_adder_4_bit_3 (
    .input1_4_bit(input_1_16_bit[7:4]), .input2_4_bit(input__16_bit[7:4]),
    .carry_in(full_adder_4_bit_4_carry_out), .carry_out(full_adder_4_bit_3_carry_out),
    .\output (\output [7:4]));
  full_adder_4_bit full_adder_4_bit_4 (
    .input1_4_bit(input_1_16_bit[3:0]), .input2_4_bit(input__16_bit[3:0]), .carry_in(carry_in),
    .carry_out(full_adder_4_bit_4_carry_out), .\output (\output [3:0]));
endmodule

module full_adder_18_bit (
  input  [17:0] in_1,
  input  [17:0] in_2,
  input  carry_in,
  output carry_out,
  output [17:0] out_5
);

  wire full_adder_1_bit_1_carry_out, full_adder_1_bit_2_carry_out;

  full_adder_16_bit full_adder_16_bit_1 (
    .input_1_16_bit(in_1[17:2]), .input__16_bit(in_2[17:2]), .carry_in(full_adder_1_bit_1_carry_out),
    .carry_out(carry_out), .\output (out_5[17:2]));
  full_adder_1_bit full_adder_1_bit_1 (
    .input_1_1_bit(in_1[1]), .input_2_1_bit(in_2[1]), .carry_in(full_adder_1_bit_2_carry_out),
    .carry_out(full_adder_1_bit_1_carry_out), .result(out_5[1]));
  full_adder_1_bit full_adder_1_bit_2 (
    .input_1_1_bit(in_1[0]), .input_2_1_bit(in_2[0]), .carry_in(carry_in),
    .carry_out(full_adder_1_bit_2_carry_out), .result(out_5[0]));
endmodule

module register (
  input  [17:0] loadingBit,
  input  enabler_bit,
  input  clock,
  input  zeroBit,
  output [17:0] outputBit
);

  wire and_1_out, or_1_out;
  wire [17:0] multiplexer_1_out;

  and and_1 (and_1_out, enabler_bit, clock);
  or or_1 (or_1_out, and_1_out, zeroBit);
  Multiplexer #(.width(18)) multiplexer_1 (
    .in0(loadingBit), .in1({18{1'b0}}), .out(multiplexer_1_out), .sel(zeroBit));  // open: en
  d_latch d_latch_1 (.Q(outputBit[0]), .\input (multiplexer_1_out[0]), .enabler(or_1_out));  // open: Q_prime
  d_latch d_latch_2 (.Q(outputBit[1]), .\input (multiplexer_1_out[1]), .enabler(or_1_out));  // open: Q_prime
  d_latch d_latch_3 (.Q(outputBit[2]), .\input (multiplexer_1_out[2]), .enabler(or_1_out));  // open: Q_prime
  d_latch d_latch_4 (.Q(outputBit[3]), .\input (multiplexer_1_out[3]), .enabler(or_1_out));  // open: Q_prime
  d_latch d_latch_5 (.Q(outputBit[4]), .\input (multiplexer_1_out[4]), .enabler(or_1_out));  // open: Q_prime
  d_latch d_latch_6 (.Q(outputBit[5]), .\input (multiplexer_1_out[5]), .enabler(or_1_out));  // open: Q_prime
  d_latch d_latch_7 (.Q(outputBit[6]), .\input (multiplexer_1_out[6]), .enabler(or_1_out));  // open: Q_prime
  d_latch d_latch_8 (.Q(outputBit[7]), .\input (multiplexer_1_out[7]), .enabler(or_1_out));  // open: Q_prime
  d_latch d_latch_9 (.Q(outputBit[8]), .\input (multiplexer_1_out[8]), .enabler(or_1_out));  // open: Q_prime
  d_latch d_latch_10 (.Q(outputBit[9]), .\input (multiplexer_1_out[9]), .enabler(or_1_out));  // open: Q_prime
  d_latch d_latch_11 (.Q(outputBit[10]), .\input (multiplexer_1_out[10]), .enabler(or_1_out));  // open: Q_prime
  d_latch d_latch_12 (.Q(outputBit[11]), .\input (multiplexer_1_out[11]), .enabler(or_1_out));  // open: Q_prime
  d_latch d_latch_13 (.Q(outputBit[12]), .\input (multiplexer_1_out[12]), .enabler(or_1_out));  // open: Q_prime
  d_latch d_latch_14 (.Q(outputBit[13]), .\input (multiplexer_1_out[13]), .enabler(or_1_out));  // open: Q_prime
  d_latch d_latch_15 (.Q(outputBit[14]), .\input (multiplexer_1_out[14]), .enabler(or_1_out));  // open: Q_prime
  d_latch d_latch_16 (.Q(outputBit[15]), .\input (multiplexer_1_out[15]), .enabler(or_1_out));  // open: Q_prime
  d_latch d_latch_17 (.Q(outputBit[16]), .\input (multiplexer_1_out[16]), .enabler(or_1_out));  // open: Q_prime
  d_latch d_latch_18 (.Q(outputBit[17]), .\input (multiplexer_1_out[17]), .enabler(or_1_out));  // open: Q_prime
endmodule

module registerList (
  input  [4:0] read2,
  input  [4:0] read,
  input  enableOutdata1,
  input  enableOutdata2,
  input  [17:0] inData1,
  input  [4:0] write1,
  input  enableInData1,
  input  registerZeroSet,
  output [17:0] outData1,
  output [17:0] outData2
);

  wire decoder_1_out0, decoder_1_out1, decoder_1_out2, decoder_1_out3, decoder_1_out4, decoder_1_out5,
       decoder_1_out6, decoder_1_out7, decoder_1_out8, decoder_1_out9, decoder_1_out10, decoder_1_out11,
       decoder_1_out12, decoder_1_out13, decoder_1_out14, decoder_1_out15, decoder_1_out16, decoder_1_out17,
       decoder_2_out0, decoder_2_out1, decoder_2_out2, decoder_2_out3, decoder_2_out4, decoder_2_out5,
       decoder_2_out6, decoder_2_out7, decoder_2_out8, decoder_2_out9, decoder_2_out10, decoder_2_out11,
       decoder_2_out12, decoder_2_out13, decoder_2_out14, decoder_2_out15, decoder_2_out16, decoder_2_out17,
       decoder_3_out0, decoder_3_out1, decoder_3_out2, decoder_3_out3, decoder_3_out4, decoder_3_out5,
       decoder_3_out6, decoder_3_out7, decoder_3_out8, decoder_3_out9, decoder_3_out10, decoder_3_out11,
       decoder_3_out12, decoder_3_out13, decoder_3_out14, decoder_3_out15, decoder_3_out16, decoder_3_out17;
  wire [17:0] controlled_buffer_1_out, controlled_buffer_2_out, register_1_outputbit, register_2_outputbit,
       register_3_outputbit, register_4_outputbit, register_5_outputbit, register_6_outputbit,
       register_7_outputbit, register_8_outputbit, register_9_outputbit, register_10_outputbit,
       register_11_outputbit, register_12_outputbit, register_13_outputbit, register_14_outputbit,
       register_15_outputbit, register_16_outputbit, register_17_outputbit, register_18_outputbit;

  Decoder #(.select(5)) decoder_1 (
    .out0(decoder_1_out0), .out1(decoder_1_out1), .out2(decoder_1_out2), .out3(decoder_1_out3),
    .out4(decoder_1_out4), .out5(decoder_1_out5), .out6(decoder_1_out6), .out7(decoder_1_out7),
    .out8(decoder_1_out8), .out9(decoder_1_out9), .out10(decoder_1_out10), .out11(decoder_1_out11),
    .out12(decoder_1_out12), .out13(decoder_1_out13), .out14(decoder_1_out14), .out15(decoder_1_out15),
    .out16(decoder_1_out16), .out17(decoder_1_out17), .sel(write1), .en(enableInData1));  // open: out18, out19, out20, out21, out22, out23, out24, out25, out26, out27, out28, out29, out30, out31
  Decoder #(.select(5), .enable("false")) decoder_2 (
    .out0(decoder_2_out0), .out1(decoder_2_out1), .out2(decoder_2_out2), .out3(decoder_2_out3),
    .out4(decoder_2_out4), .out5(decoder_2_out5), .out6(decoder_2_out6), .out7(decoder_2_out7),
    .out8(decoder_2_out8), .out9(decoder_2_out9), .out10(decoder_2_out10), .out11(decoder_2_out11),
    .out12(decoder_2_out12), .out13(decoder_2_out13), .out14(decoder_2_out14), .out15(decoder_2_out15),
    .out16(decoder_2_out16), .out17(decoder_2_out17), .sel(read2));  // open: out18, out19, out20, out21, out22, out23, out24, out25, out26, out27, out28, out29, out30, out31
  register register_1 (
    .loadingBit(inData1), .enabler_bit(decoder_1_out0), .clock(registerZeroSet), .zeroBit(registerZeroSet),
    .outputBit(register_1_outputbit));
  register register_2 (
    .loadingBit(inData1), .enabler_bit(decoder_1_out1), .clock(registerZeroSet), .zeroBit(registerZeroSet),
    .outputBit(register_2_outputbit));
  register register_3 (
    .loadingBit(inData1), .enabler_bit(decoder_1_out2), .clock(registerZeroSet), .zeroBit(registerZeroSet),
    .outputBit(register_3_outputbit));
  register register_4 (
    .loadingBit(inData1), .enabler_bit(decoder_1_out3), .clock(registerZeroSet), .zeroBit(registerZeroSet),
    .outputBit(register_4_outputbit));
  register register_5 (
    .loadingBit(inData1), .enabler_bit(decoder_1_out4), .clock(registerZeroSet), .zeroBit(registerZeroSet),
    .outputBit(register_5_outputbit));
  register register_6 (
    .loadingBit(inData1), .enabler_bit(decoder_1_out5), .clock(registerZeroSet), .zeroBit(registerZeroSet),
    .outputBit(register_6_outputbit));
  register register_7 (
    .loadingBit(inData1), .enabler_bit(decoder_1_out6), .clock(registerZeroSet), .zeroBit(registerZeroSet),
    .outputBit(register_7_outputbit));
  register register_8 (
    .loadingBit(inData1), .enabler_bit(decoder_1_out7), .clock(registerZeroSet), .zeroBit(registerZeroSet),
    .outputBit(register_8_outputbit));
  register register_9 (
    .loadingBit(inData1), .enabler_bit(decoder_1_out8), .clock(registerZeroSet), .zeroBit(registerZeroSet),
    .outputBit(register_9_outputbit));
  register register_10 (
    .loadingBit(inData1), .enabler_bit(decoder_1_out9), .clock(registerZeroSet), .zeroBit(registerZeroSet),
    .outputBit(register_10_outputbit));
  register register_11 (
    .loadingBit(inData1), .enabler_bit(decoder_1_out10), .clock(registerZeroSet), .zeroBit(registerZeroSet),
    .outputBit(register_11_outputbit));
  register register_12 (
    .loadingBit(inData1), .enabler_bit(decoder_1_out11), .clock(registerZeroSet), .zeroBit(registerZeroSet),
    .outputBit(register_12_outputbit));
  register register_13 (
    .loadingBit(inData1), .enabler_bit(decoder_1_out12), .clock(registerZeroSet), .zeroBit(registerZeroSet),
    .outputBit(register_13_outputbit));
  register register_14 (
    .loadingBit(inData1), .enabler_bit(decoder_1_out13), .clock(registerZeroSet), .zeroBit(registerZeroSet),
    .outputBit(register_14_outputbit));
  register register_15 (
    .loadingBit(inData1), .enabler_bit(decoder_1_out14), .clock(registerZeroSet), .zeroBit(registerZeroSet),
    .outputBit(register_15_outputbit));
  register register_16 (
    .loadingBit(inData1), .enabler_bit(decoder_1_out15), .clock(registerZeroSet),
    .outputBit(register_16_outputbit));  // open: zeroBit
  register register_17 (
    .loadingBit(inData1), .enabler_bit(decoder_1_out16), .clock(registerZeroSet), .zeroBit(registerZeroSet),
    .outputBit(register_17_outputbit));
  register register_18 (
    .loadingBit(inData1), .enabler_bit(decoder_1_out17), .clock(registerZeroSet), .zeroBit(registerZeroSet),
    .outputBit(register_18_outputbit));
  assign controlled_buffer_1_out = decoder_3_out0 ? register_1_outputbit : 18'bz;  // Controlled_Buffer controlled_buffer_1
  assign controlled_buffer_2_out = decoder_2_out0 ? register_1_outputbit : 18'bz;  // Controlled_Buffer controlled_buffer_2
  assign controlled_buffer_1_out = decoder_3_out1 ? register_2_outputbit : 18'bz;  // Controlled_Buffer controlled_buffer_3
  assign controlled_buffer_2_out = decoder_2_out1 ? register_2_outputbit : 18'bz;  // Controlled_Buffer controlled_buffer_4
  assign controlled_buffer_1_out = decoder_3_out2 ? register_3_outputbit : 18'bz;  // Controlled_Buffer controlled_buffer_5
  assign controlled_buffer_2_out = decoder_2_out2 ? register_3_outputbit : 18'bz;  // Controlled_Buffer controlled_buffer_6
  assign controlled_buffer_1_out = decoder_3_out3 ? register_4_outputbit : 18'bz;  // Controlled_Buffer controlled_buffer_7
  assign controlled_buffer_2_out = decoder_2_out3 ? register_4_outputbit : 18'bz;  // Controlled_Buffer controlled_buffer_8
  assign controlled_buffer_1_out = decoder_3_out4 ? register_5_outputbit : 18'bz;  // Controlled_Buffer controlled_buffer_9
  assign controlled_buffer_2_out = decoder_2_out4 ? register_5_outputbit : 18'bz;  // Controlled_Buffer controlled_buffer_10
  assign controlled_buffer_1_out = decoder_3_out5 ? register_6_outputbit : 18'bz;  // Controlled_Buffer controlled_buffer_11
  assign controlled_buffer_2_out = decoder_2_out5 ? register_6_outputbit : 18'bz;  // Controlled_Buffer controlled_buffer_12
  assign controlled_buffer_1_out = decoder_3_out6 ? register_7_outputbit : 18'bz;  // Controlled_Buffer controlled_buffer_13
  assign controlled_buffer_2_out = decoder_2_out6 ? register_7_outputbit : 18'bz;  // Controlled_Buffer controlled_buffer_14
  assign controlled_buffer_1_out = decoder_3_out7 ? register_8_outputbit : 18'bz;  // Controlled_Buffer controlled_buffer_15
  assign controlled_buffer_2_out = decoder_2_out7 ? register_8_outputbit : 18'bz;  // Controlled_Buffer controlled_buffer_16
  assign controlled_buffer_1_out = decoder_3_out8 ? register_9_outputbit : 18'bz;  // Controlled_Buffer controlled_buffer_17
  assign controlled_buffer_2_out = decoder_2_out8 ? register_9_outputbit : 18'bz;  // Controlled_Buffer controlled_buffer_18
  assign controlled_buffer_1_out = decoder_3_out9 ? register_10_outputbit : 18'bz;  // Controlled_Buffer controlled_buffer_19
  assign controlled_buffer_2_out = decoder_2_out9 ? register_10_outputbit : 18'bz;  // Controlled_Buffer controlled_buffer_20
  assign controlled_buffer_1_out = decoder_3_out10 ? register_11_outputbit : 18'bz;  // Controlled_Buffer controlled_buffer_21
  assign controlled_buffer_2_out = decoder_2_out10 ? register_11_outputbit : 18'bz;  // Controlled_Buffer controlled_buffer_22
  assign controlled_buffer_1_out = decoder_3_out11 ? register_12_outputbit : 18'bz;  // Controlled_Buffer controlled_buffer_23
  Controlled_Buffer #(.width(18)) controlled_buffer_24 (
    .out(controlled_buffer_2_out), .en(decoder_2_out11));  // open: in
  assign controlled_buffer_1_out = decoder_3_out12 ? register_13_outputbit : 18'bz;  // Controlled_Buffer controlled_buffer_25
  assign controlled_buffer_2_out = decoder_2_out12 ? register_13_outputbit : 18'bz;  // Controlled_Buffer controlled_buffer_26
  assign controlled_buffer_1_out = decoder_3_out14 ? register_14_outputbit : 18'bz;  // Controlled_Buffer controlled_buffer_27
  assign controlled_buffer_2_out = decoder_2_out13 ? register_14_outputbit : 18'bz;  // Controlled_Buffer controlled_buffer_28
  assign controlled_buffer_1_out = decoder_3_out13 ? register_15_outputbit : 18'bz;  // Controlled_Buffer controlled_buffer_29
  assign controlled_buffer_2_out = decoder_2_out14 ? register_15_outputbit : 18'bz;  // Controlled_Buffer controlled_buffer_30
  assign controlled_buffer_1_out = decoder_3_out15 ? register_16_outputbit : 18'bz;  // Controlled_Buffer controlled_buffer_31
  assign controlled_buffer_2_out = decoder_2_out15 ? register_16_outputbit : 18'bz;  // Controlled_Buffer controlled_buffer_32
  assign controlled_buffer_1_out = decoder_3_out16 ? register_17_outputbit : 18'bz;  // Controlled_Buffer controlled_buffer_33
  assign controlled_buffer_2_out = decoder_2_out16 ? register_17_outputbit : 18'bz;  // Controlled_Buffer controlled_buffer_34
  assign controlled_buffer_1_out = decoder_3_out17 ? register_18_outputbit : 18'bz;  // Controlled_Buffer controlled_buffer_35
  assign controlled_buffer_2_out = decoder_2_out17 ? register_18_outputbit : 18'bz;  // Controlled_Buffer controlled_buffer_36
  assign outData1 = enableOutdata1 ? controlled_buffer_1_out : 18'bz;  // Controlled_Buffer controlled_buffer_37
  assign outData2 = enableOutdata2 ? controlled_buffer_2_out : 18'bz;  // Controlled_Buffer controlled_buffer_38
  Decoder #(.select(5), .enable("false")) decoder_3 (
    .out0(decoder_3_out0), .out1(decoder_3_out1), .out2(decoder_3_out2), .out3(decoder_3_out3),
    .out4(decoder_3_out4), .out5(decoder_3_out5), .out6(decoder_3_out6), .out7(decoder_3_out7),
    .out8(decoder_3_out8), .out9(decoder_3_out9), .out10(decoder_3_out10), .out11(decoder_3_out11),
    .out12(decoder_3_out12), .out13(decoder_3_out13), .out14(decoder_3_out14), .out15(decoder_3_out15),
    .out16(decoder_3_out16), .out17(decoder_3_out17), .sel(read));  // open: out18, out19, out20, out21, out22, out23, out24, out25, out26, out27, out28, out29, out30, out31
endmodule

module alu (
  input  [17:0] input_1_18_bit,
  input  [17:0] input_2_18_bit,
  input  selection_bit_1,
  input  selection_bit_2
);

  wire undriven_7;
  wire [17:0] multiplexer_1_out, undriven, undriven_2, undriven_3, undriven_4, undriven_5, undriven_6,
       undriven_8, undriven_9;

  full_adder_18_bit full_adder_18_bit_1 (.in_1(undriven_2), .in_2(undriven));  // open: carry_in, carry_out, out_5
  Multiplexer #(.width(18)) multiplexer_1 (
    .in0(input_1_18_bit), .in1(input_2_18_bit), .out(multiplexer_1_out), .sel(undriven_7),
    .en(selection_bit_2));
  // AND_Gate and_1 has open pins: in0=undriven_3, in1=undriven_4, out=open
  // NOR_Gate nor_1 has open pins: in0=undriven_5, in1=undriven_6, out=open
  // NAND_Gate nand_1 has open pins: in0=undriven_8, in1=undriven_9, out=open
endmodule
