// Logisim project d latch.circ as structural Verilog: 2 circuits, main circuit d-latch
module d_latch (
  input  D,
  input  enable,
  output Q,
  output Q_prime
);

  wire nand_1_out, nand_2_out, nand_3_out, nand_4_out;

  nand nand_1 (nand_1_out, D, enable);
  nand nand_2 (nand_2_out, enable, D);
  nand nand_3 (nand_3_out, nand_1_out, nand_4_out);
  nand nand_4 (nand_4_out, nand_3_out, nand_2_out);
endmodule

module d_flip_flop (
  input  d,
  output q,
  output q_prime
);

  wire clock_1_out, d_latch_1_q, not_1_out, not_2_out;

  Clock clock_1 (.out(clock_1_out));
  d_latch d_latch_1 (.D(d), .Q(d_latch_1_q), .enable(not_1_out));  // open: Q_prime
  not not_1 (not_1_out, clock_1_out);
  not not_2 (not_2_out, not_1_out);
  d_latch d_latch_2 (.D(d_latch_1_q), .Q(q), .Q_prime(q_prime), .enable(not_2_out));
endmodule
